# Fritzing sketch BaoQuyDiep-Latest (saved by Fritzing 0.9.3b)
circuit board: 8.46667cm x 5.64444cm
breadboards: 1

parts:
  MCP9808 = MCP9808 High Accuracy I2C Temperature Sensor [part_number=1782]
  Raspberry_Pi_1 = Raspberry Pi 3 [part_number=RPI-3-V1.2]

nets:
  VDD: MCP9808.VDD, Raspberry_Pi_1.3v3
  GND: MCP9808.GND, Raspberry_Pi_1.GND
  N1: MCP9808.SCL, Raspberry_Pi_1.GPIO3
  N2: MCP9808.SDA, Raspberry_Pi_1.GPIO2

notes:
  BAO QUY

custom parts:
  MCP9808 High Accuracy I2C Temperature Sensor: This I2C digital temperature sensor is one of the more accurate/precise we've ever seen, with a typical accuracy of ±0.25°C over the sensor's -40°C to +125°C range and precision of +0.0625°C. They work great with any microcontroller using standard i2c. There are 3 address pins so you can connect up to 8 to a single I2C bus without address collisions. Best of all, a wide voltage range makes is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
